# Fritzing sketch arduino_humiditylogger (saved by Fritzing 0.9.0b)
breadboards: 1

parts:
  Part1 = Arduino Uno (Rev3)
  U1 = HIH-4030 [package=hih-4030]
  U2 = TEMPERATURE-SENSOR [package=to-92]  # not connected
  Part2 = Arduino Ethernet Shield (Rev3)  # not connected

nets:
  N1: Part1.A0, U1.OUT
  5V: Part1.5V, U1.VCC
  GND: Part1.GND, U1.GND
